// Logisim project final_computer_simulation.circ as structural Verilog: 15 circuits, main circuit Memory Cell
// DFF
module Memory_Cell (
  input  clock,
  input  WE,
  input  Din,
  input  OE,
  input  Reset,
  output Dout,
  output Stored_data
);

  wire and_1_out, and_2_out, not_1_out, or_1_out;

  not not_1 (not_1_out, WE);
  and and_1 (and_1_out, Stored_data, not_1_out);
  and and_2 (and_2_out, WE, Din);
  or or_1 (or_1_out, and_1_out, and_2_out);
  D_Flip_Flop d_ff_1 (.clk(clock), .D(or_1_out), .Q(Stored_data), .reset(Reset));  // open: Qn, preset, en
  assign Dout = OE ? Stored_data : 1'bz;  // Controlled_Buffer controlled_buffer_1
endmodule

module register (
  input  Clock,
  input  WE,
  input  [7:0] Din,
  input  OE,
  input  Reset,
  output [7:0] Dout,
  output [7:0] Stored_Data
);

  Memory_Cell memory_cell_1 (
    .clock(Clock), .WE(WE), .Din(Din[0]), .OE(OE), .Reset(Reset), .Dout(Dout[0]), .Stored_data(Stored_Data[0]));
  Memory_Cell memory_cell_2 (
    .clock(Clock), .WE(WE), .Din(Din[1]), .OE(OE), .Reset(Reset), .Dout(Dout[1]), .Stored_data(Stored_Data[1]));
  Memory_Cell memory_cell_3 (
    .clock(Clock), .WE(WE), .Din(Din[2]), .OE(OE), .Reset(Reset), .Dout(Dout[2]), .Stored_data(Stored_Data[2]));
  Memory_Cell memory_cell_4 (
    .clock(Clock), .WE(WE), .Din(Din[3]), .OE(OE), .Reset(Reset), .Dout(Dout[3]), .Stored_data(Stored_Data[3]));
  Memory_Cell _4 (
    .clock(Clock), .WE(WE), .Din(Din[4]), .OE(OE), .Reset(Reset), .Dout(Dout[4]), .Stored_data(Stored_Data[4]));
  Memory_Cell _5 (
    .clock(Clock), .WE(WE), .Din(Din[5]), .OE(OE), .Reset(Reset), .Dout(Dout[5]), .Stored_data(Stored_Data[5]));
  Memory_Cell _6 (
    .clock(Clock), .WE(WE), .Din(Din[6]), .OE(OE), .Reset(Reset), .Dout(Dout[6]), .Stored_data(Stored_Data[6]));
  Memory_Cell _7 (
    .clock(Clock), .WE(WE), .Din(Din[7]), .OE(OE), .Reset(Reset), .Dout(Dout[7]), .Stored_data(Stored_Data[7]));
endmodule

module MAR (
  input  Clock,
  input  WE,
  input  [3:0] Din,
  input  OE,
  input  Reset,
  output [3:0] Dout,
  output [3:0] Stored_Data
);

  Memory_Cell memory_cell_1 (
    .clock(Clock), .WE(WE), .Din(Din[0]), .OE(OE), .Reset(Reset), .Dout(Dout[0]), .Stored_data(Stored_Data[0]));
  Memory_Cell memory_cell_2 (
    .clock(Clock), .WE(WE), .Din(Din[1]), .OE(OE), .Reset(Reset), .Dout(Dout[1]), .Stored_data(Stored_Data[1]));
  Memory_Cell memory_cell_3 (
    .clock(Clock), .WE(WE), .Din(Din[2]), .OE(OE), .Reset(Reset), .Dout(Dout[2]), .Stored_data(Stored_Data[2]));
  Memory_Cell memory_cell_4 (
    .clock(Clock), .WE(WE), .Din(Din[3]), .OE(OE), .Reset(Reset), .Dout(Dout[3]), .Stored_data(Stored_Data[3]));
endmodule

// Adder
module Full_Adder (
  input  A,
  input  B,
  input  Cin,
  output Sum,
  output Cout
);

  wire and_1_out, and_2_out, xor_1_out;

  xor xor_1 (xor_1_out, A, B);
  and and_1 (and_1_out, A, B);
  and and_2 (and_2_out, Cin, xor_1_out);
  or or_1 (Cout, and_1_out, and_2_out);
  xor xor_2 (Sum, xor_1_out, Cin);
endmodule

module CPU (
  input  Load,
  input  OE_Test_data,
  input  [3:0] in_3,
  input  Reset,
  input  [7:0] in_5,
  input  in_6,
  input  Reset_2,
  output [3:0] out_8,
  output Count_Enable,
  output Counter_OE,
  output [7:0] out_11,
  output [3:0] out_12,
  output WE,
  output OE,
  output WE_2,
  output OE_2,
  output WE_3,
  output [7:0] out_18,
  output OE_3,
  output [3:0] out_20,
  output Internal_OE,
  output WE_4,
  output OE_4,
  output WE_5,
  output [7:0] out_25,
  output [7:0] out_26,
  output [7:0] out_27,
  output OE_5,
  output out_29,
  output [3:0] out_30,
  output WE_6,
  output OE_6,
  output WE_7,
  output [7:0] out_34,
  output [7:0] out_35,
  output [2:0] out_36
);

  wire a_output_enable, \and , b_output_enable, clock_1_out, \or , sub, \xor ;
  wire [3:0] decimal_decoder_2_dout, decimal_decoder_2_dout_2, decimal_decoder_2_dout_3,
       decimal_decoder_2_dout_4, decimal_decoder_2_dout_5, decimal_decoder_2_dout_6,
       decimal_decoder_2_dout_7, decimal_decoder_2_dout_8, MAR_dout;
  wire [7:0] ALU_dout, bit_extender_1_out, bit_extender_2_out;
  wire [15:0] decimal_decoder_3_dout, decimal_decoder_3_dout_2;
  wire [31:0] decimal_decoder_1_dout, decimal_decoder_4_dout, decimal_decoder_5_dout;

  Counter #(.width(4), .max('h3)) Counter_Aw (
    .load(Load), .D(out_8), .count(Count_Enable), .Q(out_12), .clk(clock_1_out), .clr(Reset));  // open: carry
  assign out_8 = Counter_OE ? out_12 : 4'bz;  // Controlled_Buffer controlled_buffer_1
  assign bit_extender_1_out = {{4{1'b0}}, out_12};  // Bit_Extender bit_extender_1
  Clock clock_1 (.out(clock_1_out));
  Decimal_Decoder decimal_decoder_1 (.Din(bit_extender_1_out), .Dout(decimal_decoder_1_dout));
  register Instruction_Register (
    .Clock(clock_1_out), .WE(WE_3), .Din(ALU_dout), .OE(OE_3), .Dout(out_11), .Stored_Data(out_18));  // open: Reset
  register A (
    .Clock(clock_1_out), .WE(WE_5), .Din(ALU_dout), .OE(a_output_enable), .Stored_Data(out_26));  // open: Reset, Dout
  register B (
    .Clock(clock_1_out), .WE(WE_7), .Din(ALU_dout), .OE(b_output_enable), .Stored_Data(out_35));  // open: Reset, Dout
  _7_Segment_Display u_7_segment_display_1 (
    .g(decimal_decoder_1_dout[3]), .f(decimal_decoder_1_dout[2]), .a(decimal_decoder_1_dout[1]),
    .b(decimal_decoder_1_dout[0]), .e(decimal_decoder_1_dout[19]), .d(decimal_decoder_1_dout[18]),
    .c(decimal_decoder_1_dout[17]), .dp(decimal_decoder_1_dout[16]));
  improved_Adder ALU (
    .XOR(\xor ), .AND(\and ), .OR(\or ), .Subtract(sub), .B(out_35), .A(out_26), .Cout(out_29),
    .Stored_Data(out_27), .Dout(ALU_dout), .OE(OE_5));
  Decimal_Decoder decimal_decoder_2 (
    .Din(out_35),
    .Dout({decimal_decoder_2_dout_8, decimal_decoder_2_dout_7, decimal_decoder_2_dout_6, decimal_decoder_2_dout_5, decimal_decoder_2_dout_4, decimal_decoder_2_dout_3, decimal_decoder_2_dout_2, decimal_decoder_2_dout}));
  Decimal_Decoder decimal_decoder_3 (.Din(out_26), .Dout({decimal_decoder_3_dout_2, decimal_decoder_3_dout}));
  BitSelector #(.group(4)) bitselector_1 (.in(out_11), .out(out_8), .sel(1'b0));
  _7_Segment_Display u_7_segment_display_2 (
    .g(decimal_decoder_3_dout[11]), .f(decimal_decoder_3_dout[10]), .a(decimal_decoder_3_dout[9]),
    .b(decimal_decoder_3_dout[8]), .e(decimal_decoder_3_dout_2[11]), .d(decimal_decoder_3_dout_2[10]),
    .c(decimal_decoder_3_dout_2[9]), .dp(decimal_decoder_3_dout_2[8]));
  _7_Segment_Display u_7_segment_display_3 (
    .g(decimal_decoder_2_dout_3[3]), .f(decimal_decoder_2_dout_3[2]), .a(decimal_decoder_2_dout_3[1]),
    .b(decimal_decoder_2_dout_3[0]), .e(decimal_decoder_2_dout_7[3]), .d(decimal_decoder_2_dout_7[2]),
    .c(decimal_decoder_2_dout_7[1]), .dp(decimal_decoder_2_dout_7[0]));
  _7_Segment_Display u_7_segment_display_4 (
    .g(decimal_decoder_3_dout[3]), .f(decimal_decoder_3_dout[2]), .a(decimal_decoder_3_dout[1]),
    .b(decimal_decoder_3_dout[0]), .e(decimal_decoder_3_dout_2[3]), .d(decimal_decoder_3_dout_2[2]),
    .c(decimal_decoder_3_dout_2[1]), .dp(decimal_decoder_3_dout_2[0]));
  _7_Segment_Display u_7_segment_display_5 (
    .g(decimal_decoder_3_dout[7]), .f(decimal_decoder_3_dout[6]), .a(decimal_decoder_3_dout[5]),
    .b(decimal_decoder_3_dout[4]), .e(decimal_decoder_3_dout_2[7]), .d(decimal_decoder_3_dout_2[6]),
    .c(decimal_decoder_3_dout_2[5]), .dp(decimal_decoder_3_dout_2[4]));
  _7_Segment_Display u_7_segment_display_6 (
    .g(decimal_decoder_2_dout[3]), .f(decimal_decoder_2_dout[2]), .a(decimal_decoder_2_dout[1]),
    .b(decimal_decoder_2_dout[0]), .e(decimal_decoder_2_dout_5[3]), .d(decimal_decoder_2_dout_5[2]),
    .c(decimal_decoder_2_dout_5[1]), .dp(decimal_decoder_2_dout_5[0]));
  _7_Segment_Display u_7_segment_display_7 (
    .g(decimal_decoder_2_dout_2[3]), .f(decimal_decoder_2_dout_2[2]), .a(decimal_decoder_2_dout_2[1]),
    .b(decimal_decoder_2_dout_2[0]), .e(decimal_decoder_2_dout_6[3]), .d(decimal_decoder_2_dout_6[2]),
    .c(decimal_decoder_2_dout_6[1]), .dp(decimal_decoder_2_dout_6[0]));
  LED D7 (.in(ALU_dout[7]));
  LED D6 (.in(ALU_dout[6]));
  LED D5 (.in(ALU_dout[5]));
  assign ALU_dout = in_6 ? in_5 : 8'bz;  // Controlled_Buffer controlled_buffer_2
  LED D3 (.in(ALU_dout[3]));
  LED D4 (.in(ALU_dout[4]));
  LED D2 (.in(ALU_dout[2]));
  LED D1 (.in(ALU_dout[1]));
  LED D0 (.in(ALU_dout[0]));
  assign ALU_dout = Internal_OE ? out_25 : 8'bz;  // Controlled_Buffer controlled_buffer_3
  MAR MAR (
    .Clock(clock_1_out), .WE(WE_2), .Din(out_8), .OE(OE_2), .Stored_Data(out_20), .Dout(MAR_dout));  // open: Reset
  register MBR (
    .Clock(clock_1_out), .WE(WE_4), .Din(ALU_dout), .OE(OE_4), .Dout(ALU_dout), .Stored_Data(out_25));  // open: Reset
  Output_Register output_register_1 (
    .OE(OE_6), .Clock(clock_1_out), .WE(WE_6), .Din(ALU_dout), .Dout(ALU_dout), .Stored_Data(out_34),
    .INC(1'b0), .CMP(1'b0), .SHL(1'b0), .SHR(1'b0));  // open: RESET
  Decimal_Decoder decimal_decoder_4 (.Din(out_34), .Dout(decimal_decoder_4_dout));
  _7_Segment_Display u_7_segment_display_8 (
    .g(decimal_decoder_4_dout[15]), .f(decimal_decoder_4_dout[14]), .a(decimal_decoder_4_dout[13]),
    .b(decimal_decoder_4_dout[12]), .e(decimal_decoder_4_dout[31]), .d(decimal_decoder_4_dout[30]),
    .c(decimal_decoder_4_dout[29]), .dp(decimal_decoder_4_dout[28]));
  _7_Segment_Display u_7_segment_display_9 (
    .g(decimal_decoder_4_dout[11]), .f(decimal_decoder_4_dout[10]), .a(decimal_decoder_4_dout[9]),
    .b(decimal_decoder_4_dout[8]), .e(decimal_decoder_4_dout[27]), .d(decimal_decoder_4_dout[26]),
    .c(decimal_decoder_4_dout[25]), .dp(decimal_decoder_4_dout[24]));
  assign MAR_dout = OE_Test_data ? in_3 : 4'bz;  // Controlled_Buffer controlled_buffer_4
  _7_Segment_Display u_7_segment_display_10 (
    .g(decimal_decoder_4_dout[3]), .f(decimal_decoder_4_dout[2]), .a(decimal_decoder_4_dout[1]),
    .b(decimal_decoder_4_dout[0]), .e(decimal_decoder_4_dout[19]), .d(decimal_decoder_4_dout[18]),
    .c(decimal_decoder_4_dout[17]), .dp(decimal_decoder_4_dout[16]));
  _7_Segment_Display u_7_segment_display_11 (
    .g(decimal_decoder_4_dout[7]), .f(decimal_decoder_4_dout[6]), .a(decimal_decoder_4_dout[5]),
    .b(decimal_decoder_4_dout[4]), .e(decimal_decoder_4_dout[23]), .d(decimal_decoder_4_dout[22]),
    .c(decimal_decoder_4_dout[21]), .dp(decimal_decoder_4_dout[20]));
  LED D6_2 (.in(ALU_dout[6]));
  LED D7_2 (.in(ALU_dout[7]));
  LED D5_2 (.in(ALU_dout[5]));
  LED D3_2 (.in(ALU_dout[3]));
  LED D4_2 (.in(ALU_dout[4]));
  LED D2_2 (.in(ALU_dout[2]));
  LED D1_2 (.in(ALU_dout[1]));
  LED D0_2 (.in(ALU_dout[0]));
  RAM #(.addrWidth(4), .bus("separate")) ram_1 (
    .addr(MAR_dout), .din(ALU_dout), .data(ALU_dout), .str(WE), .clk(clock_1_out), .ld(OE));  // open: sel, clr
  BitSelector #(.group(4)) bitselector_2 (.in(out_18), .out(out_30), .sel(1'b1));
  Counter #(.width(3), .max('h5)) sck_cont (
    .Q(out_36), .clk(clock_1_out), .clr(Reset_2));  // open: load, D, count, carry
  assign bit_extender_2_out = {{5{1'b0}}, out_36};  // Bit_Extender bit_extender_2
  CU1 cu1_1 (
    .OPC3(out_30[3]), .OPC2(out_30[2]), .OPC1(out_30[1]), .OPC0(out_30[0]), .SC2(out_36[2]), .SC1(out_36[1]),
    .SC0(out_36[0]), .C0(Counter_OE), .C1(Count_Enable), .C2(WE), .C3(OE), .C4(WE_4), .C5(Internal_OE),
    .C6(OE_4), .C7(WE_3), .C8(OE_3), .C9(WE_2), .C10(OE_2), .C11(OE_5));
  CU2 cu2_1 (
    .OP3(out_30[3]), .OP2(out_30[2]), .OP1(out_30[1]), .OP0(out_30[0]), .SC2(out_36[2]), .SC1(out_36[1]),
    .SC0(out_36[0]), .C12(WE_5), .C13(WE_7), .C14(OE_6), .C15(WE_6), .C16(sub), .C17(\xor ), .C18(\and ),
    .C19(\or ), .C20(a_output_enable), .C21(b_output_enable));
  Decimal_Decoder decimal_decoder_5 (.Din(bit_extender_2_out), .Dout(decimal_decoder_5_dout));
  _7_Segment_Display u_7_segment_display_12 (
    .g(decimal_decoder_5_dout[3]), .f(decimal_decoder_5_dout[2]), .a(decimal_decoder_5_dout[1]),
    .b(decimal_decoder_5_dout[0]), .e(decimal_decoder_5_dout[19]), .d(decimal_decoder_5_dout[18]),
    .c(decimal_decoder_5_dout[17]), .dp(decimal_decoder_5_dout[16]));
endmodule

// ALU
module _8_bit_adder (
  input  Cin,
  input  [7:0] A,
  input  OE,
  input  in_4,
  input  [7:0] B,
  output [7:0] Dout,
  output [7:0] ALU_Result,
  output Cout
);

  wire full_adder_1_cout, full_adder_2_cout, full_adder_3_cout, full_adder_4_cout, full_adder_5_cout,
       full_adder_6_cout, full_adder_7_cout, xor_1_out, xor_2_out, xor_3_out, xor_4_out, xor_5_out,
       xor_6_out, xor_7_out, xor_8_out;

  xor xor_1 (xor_1_out, in_4, B[1]);
  xor xor_2 (xor_2_out, in_4, B[0]);
  xor xor_3 (xor_3_out, in_4, B[3]);
  xor xor_4 (xor_4_out, in_4, B[2]);
  xor xor_5 (xor_5_out, in_4, B[4]);
  xor xor_6 (xor_6_out, in_4, B[5]);
  xor xor_7 (xor_7_out, in_4, B[7]);
  xor xor_8 (xor_8_out, in_4, B[6]);
  Full_Adder full_adder_1 (.A(A[0]), .B(xor_2_out), .Cin(Cin), .Sum(ALU_Result[0]), .Cout(full_adder_1_cout));
  Full_Adder full_adder_2 (
    .A(A[1]), .B(xor_1_out), .Cin(full_adder_1_cout), .Sum(ALU_Result[1]), .Cout(full_adder_2_cout));
  Full_Adder full_adder_3 (
    .A(A[2]), .B(xor_4_out), .Cin(full_adder_2_cout), .Sum(ALU_Result[2]), .Cout(full_adder_3_cout));
  Full_Adder full_adder_4 (
    .A(A[3]), .B(xor_3_out), .Cin(full_adder_3_cout), .Sum(ALU_Result[3]), .Cout(full_adder_4_cout));
  Full_Adder full_adder_5 (
    .A(A[4]), .B(xor_5_out), .Cin(full_adder_4_cout), .Sum(ALU_Result[4]), .Cout(full_adder_5_cout));
  Full_Adder full_adder_6 (
    .A(A[5]), .B(xor_6_out), .Cin(full_adder_5_cout), .Sum(ALU_Result[5]), .Cout(full_adder_6_cout));
  Full_Adder full_adder_7 (
    .A(A[6]), .B(xor_8_out), .Cin(full_adder_6_cout), .Sum(ALU_Result[6]), .Cout(full_adder_7_cout));
  Full_Adder full_adder_8 (.A(A[7]), .B(xor_7_out), .Cin(full_adder_7_cout), .Sum(ALU_Result[7]), .Cout(Cout));
  assign Dout = OE ? ALU_Result : 8'bz;  // Controlled_Buffer controlled_buffer_1
endmodule

module Ripple_Counter (
  input  in_1,
  input  Count_Enable,
  input  RESET,
  output [3:0] out_4
);

  T_Flip_Flop #(.trigger("falling")) t_ff_1 (
    .clk(in_1), .T(1'b1), .Q(out_4[0]), .reset(RESET), .en(Count_Enable));  // open: Qn, preset
  T_Flip_Flop #(.trigger("falling")) t_ff_2 (
    .clk(out_4[0]), .T(1'b1), .Q(out_4[1]), .reset(RESET), .en(Count_Enable));  // open: Qn, preset
  T_Flip_Flop #(.trigger("falling")) t_ff_3 (
    .clk(out_4[1]), .T(1'b1), .Q(out_4[2]), .reset(RESET), .en(Count_Enable));  // open: Qn, preset
  T_Flip_Flop #(.trigger("falling")) t_ff_4 (
    .clk(out_4[2]), .T(1'b1), .Q(out_4[3]), .reset(RESET), .en(Count_Enable));  // open: Qn, preset
endmodule

module Decimal_Decoder (
  input  [7:0] Din,
  output [31:0] Dout
);

  ROM #(.dataWidth(32)) rom_1 (
    .addr(Din),
    .data({Dout[31:28], Dout[15:12], Dout[27:24], Dout[11:8], Dout[23:20], Dout[7:4], Dout[19:16], Dout[3:0]}));  // open: sel

  // Notes on the sheet:
  //   contents of rom_1 (hex, n*v repeats v):
  //   e7 21 cb 6b 2d 6e ee 23 ef 2f 21e7 2121 21cb 216b 212d 216e 21ee 2123 21ef 212f cbe7 cb21 cbcb cb6b
  //   cb2d cb6e cbee cb23 cbef cb2f 6be7 6b21 6bcb 6b6b 6b2d 6b6e 6bee 6b23 6bef 6b2f 2de7 2d21 2dcb 2d6b
  //   2d2d 2d6e 2dee 2d23 2def 2d2f 6ee7 6e21 6ecb 6e6b 6e2d 6e6e 6eee 6e23 6eef 6e2f eee7 ee21 eecb ee6b
  //   ee2d ee6e eeee ee23 eeef ee2f 23e7 2321 23cb 236b 232d 236e 23ee 2323 23ef 232f efe7 ef21 efcb ef6b
  //   ef2d ef6e efee ef23 efef ef2f 2fe7 2f21 2fcb 2f6b 2f2d 2f6e 2fee 2f23 2fef 2f2f 21e7e7 21e721 21e7cb
  //   21e76b 21e72d 21e76e 21e7ee 21e723 21e7ef 21e72f 2121e7 212121 2121cb 21216b 21212d 21216e 2121ee
  //   212123 2121ef 21212f 21cbe7 21cb21 21cbcb 21cb6b 21cb2d 21cb6e 21cbee 21cb23 21cbef 21cb2f 216be7
  //   216b21 216bcb 216b6b 216b2d 216b6e 216bee 216b23 216bef 216b2f 212de7 212d21 212dcb 212d6b 212d2d
  //   212d6e 212dee 212d23 212def 212d2f 216ee7 216e21 216ecb 216e6b 216e2d 216e6e 216eee 216e23 216eef
  //   216e2f 21eee7 21ee21 21eecb 21ee6b 21ee2d 21ee6e 21eeee 21ee23 21eeef 21ee2f 2123e7 212321 2123cb
  //   21236b 21232d 21236e 2123ee 212323 2123ef 21232f 21efe7 21ef21 21efcb 21ef6b 21ef2d 21ef6e 21efee
  //   21ef23 21efef 21ef2f 212fe7 212f21 212fcb 212f6b 212f2d 212f6e 212fee 212f23 212fef 212f2f cbe7e7
  //   cbe721 cbe7cb cbe76b cbe72d cbe76e cbe7ee cbe723 cbe7ef cbe72f cb21e7 cb2121 cb21cb cb216b cb212d
  //   cb216e cb21ee cb2123 cb21ef cb212f cbcbe7 cbcb21 cbcbcb cbcb6b cbcb2d cbcb6e cbcbee cbcb23 cbcbef
  //   cbcb2f cb6be7 cb6b21 cb6bcb cb6b6b cb6b2d cb6b6e cb6bee cb6b23 cb6bef cb6b2f cb2de7 cb2d21 cb2dcb
  //   cb2d6b cb2d2d cb2d6e cb2dee cb2d23 cb2def cb2d2f cb6ee7 cb6e21 cb6ecb cb6e6b cb6e2d cb6e6e
endmodule

module Control_Unit (
  input  OPC3,
  input  OPC2,
  input  OPC1,
  input  OPC0,
  input  SC2,
  input  SC1,
  input  SC0,
  output C0,
  output C1,
  output C2,
  output C3,
  output C4,
  output C5,
  output C6,
  output C7,
  output C8,
  output C9,
  output C10,
  output C11
);

  wire and_5_out, and_6_out, and_7_out, and_8_out, and_9_out, and_10_out, and_11_out, and_13_out, and_14_out,
       and_15_out, and_16_out, and_17_out, and_18_out, and_19_out, not_1_out, not_2_out, not_3_out,
       not_4_out, not_5_out, not_6_out, not_7_out, not_8_out, not_9_out, not_10_out, not_11_out, not_12_out,
       not_13_out, not_14_out, not_15_out, not_16_out, not_17_out, not_18_out, not_19_out, not_20_out,
       not_21_out, not_22_out, not_23_out, not_24_out;

  not not_1 (not_1_out, SC2);
  not not_2 (not_2_out, SC1);
  not not_3 (not_3_out, SC0);
  not not_4 (not_4_out, SC2);
  not not_5 (not_5_out, SC1);
  and and_1 (C2, OPC1, SC2);
  not not_6 (not_6_out, SC2);
  not not_7 (not_7_out, SC1);
  not not_8 (not_8_out, OPC1);
  not not_9 (not_9_out, SC0);
  not not_10 (not_10_out, SC2);
  not not_11 (not_11_out, SC1);
  not not_12 (not_12_out, OPC1);
  not not_13 (not_13_out, SC0);
  not not_14 (not_14_out, SC0);
  and and_2 (C6, OPC1, SC2);
  not not_15 (not_15_out, SC0);
  not not_16 (not_16_out, OPC1);
  not not_17 (not_17_out, SC2);
  not not_18 (not_18_out, SC1);
  not not_19 (not_19_out, SC0);
  not not_20 (not_20_out, OPC1);
  not not_21 (not_21_out, SC2);
  not not_22 (not_22_out, SC1);
  not not_23 (not_23_out, SC0);
  not not_24 (not_24_out, OPC0);
  and and_3 (C0, not_1_out, not_2_out, not_3_out);
  and and_4 (C1, not_4_out, not_5_out, SC0);
  and and_5 (and_5_out, not_6_out, not_7_out, SC0);
  and and_6 (and_6_out, not_8_out, SC2, not_9_out);
  and and_7 (and_7_out, not_10_out, not_11_out, SC0);
  and and_8 (and_8_out, not_12_out, SC2, not_13_out);
  and and_9 (and_9_out, OPC1, OPC0, SC0);
  and and_10 (and_10_out, SC1, not_14_out);
  and and_11 (and_11_out, SC2, SC0);
  and and_12 (C7, SC1, not_15_out);
  and and_13 (and_13_out, not_16_out, SC1, SC0);
  and and_14 (and_14_out, OPC0, SC1, SC0);
  and and_15 (and_15_out, not_17_out, not_18_out, not_19_out);
  and and_16 (and_16_out, not_20_out, SC1, SC0);
  and and_17 (and_17_out, OPC0, SC1, SC0);
  and and_18 (and_18_out, not_21_out, not_22_out, SC0);
  and and_19 (and_19_out, SC2, not_23_out);
  and and_20 (C11, OPC1, not_24_out, SC1, SC0);
  or or_1 (C3, and_5_out, and_6_out);
  or or_2 (C4, and_7_out, and_8_out, and_9_out);
  or or_3 (C5, and_10_out, and_11_out);
  or or_4 (C8, and_13_out, and_14_out);
  or or_5 (C9, and_15_out, and_16_out, and_17_out);
  or or_6 (C10, and_18_out, and_19_out);
endmodule

module Second_Control_Unit (
  input  OPC3,
  input  OPC2,
  input  OPC1,
  input  OPC0,
  input  SC2,
  input  SC1,
  input  SC0,
  output C12,
  output C13,
  output C14,
  output C15
);

  wire not_1_out, not_2_out;

  not not_1 (not_1_out, OPC0);
  and and_1 (C13, OPC0, SC2, SC0);
  and and_2 (C14, OPC1, OPC0, SC1, SC0);
  not not_2 (not_2_out, OPC0);
  and and_3 (C12, not_1_out, SC2, SC0);
  and and_4 (C15, OPC1, not_2_out, SC1, SC0);
endmodule

module new_output (
  input  [7:0] in_1,
  output [13:0] out_2
);

  wire [31:0] rom_1_data;

  assign out_2 = {{6{1'b0}}, in_1};  // Bit_Extender bit_extender_1
  ROM #(.addrWidth(14), .dataWidth(32)) rom_1 (.addr(out_2), .data(rom_1_data));  // open: sel
  _7_Segment_Display u_7_segment_display_1 (
    .g(rom_1_data[27]), .f(rom_1_data[26]), .a(rom_1_data[25]), .b(rom_1_data[24]), .e(rom_1_data[31]),
    .d(rom_1_data[30]), .c(rom_1_data[29]), .dp(rom_1_data[28]));
  _7_Segment_Display u_7_segment_display_2 (
    .g(rom_1_data[19]), .f(rom_1_data[18]), .a(rom_1_data[17]), .b(rom_1_data[16]), .e(rom_1_data[23]),
    .d(rom_1_data[22]), .c(rom_1_data[21]), .dp(rom_1_data[20]));
  _7_Segment_Display u_7_segment_display_3 (
    .g(rom_1_data[11]), .f(rom_1_data[10]), .a(rom_1_data[9]), .b(rom_1_data[8]), .e(rom_1_data[15]),
    .d(rom_1_data[14]), .c(rom_1_data[13]), .dp(rom_1_data[12]));
  _7_Segment_Display u_7_segment_display_4 (
    .g(rom_1_data[3]), .f(rom_1_data[2]), .a(rom_1_data[1]), .b(rom_1_data[0]), .e(rom_1_data[7]),
    .d(rom_1_data[6]), .c(rom_1_data[5]), .dp(rom_1_data[4]));

  // Notes on the sheet:
  //   contents of rom_1 (hex, n*v repeats v):
  //   e7 21 cb 6b 2d 6e ee 23 ef 6f 21e7 2121 21cb 216b 212d 216e 21ee 2123 21ef 216f cbe7 cb21 cbcb cb6b
  //   cb2d cb6e cbee cb23 cbef cb6f 6be7 6b21 6bcb 6b6b 6b2d 6b6e 6bee 6b23 6bef 6b6f 2de7 2d21 2dcb 2d6b
  //   2d2d 2d6e 2dee 2d23 2def 2d6f 6ee7 6e21 6ecb 6e6b 6e2d 6e6e 6eee 6e23 6eef 6e6f eee7 ee21 eecb ee6b
  //   ee2d ee6e eeee ee23 eeef ee6f 23e7 2321 23cb 236b 232d 236e 23ee 2323 23ef 236f efe7 ef21 efcb ef6b
  //   ef2d ef6e efee ef23 efef ef6f 6fe7 6f21 6fcb 6f6b 6f2d 6f6e 6fee 6f23 6fef 6f6f 21e7e7 21e721 21e7cb
  //   21e76b 21e72d 21e76e 21e7ee 21e723 21e7ef 21e76f 2121e7 212121 2121cb 21216b 21212d 21216e 2121ee
  //   212123 2121ef 21216f 21cbe7 21cb21 21cbcb 21cb6b 21cb2d 21cb6e 21cbee 21cb23 21cbef 21cb6f 216be7
  //   216b21 216bcb 216b6b 216b2d 216b6e 216bee 216b23 216bef 216b6f 212de7 212d21 212dcb 212d6b 212d2d
  //   212d6e 212dee 212d23 212def 212d6f 216ee7 216e21 216ecb 216e6b 216e2d 216e6e 216eee 216e23 216eef
  //   216e6f 21eee7 21ee21 21eecb 21ee6b 21ee2d 21ee6e 21eeee 21ee23 21eeef 21ee6f 2123e7 212321 2123cb
  //   21236b 21232d 21236e 2123ee 212323 2123ef 21236f 21efe7 21ef21 21efcb 21ef6b 21ef2d 21ef6e 21efee
  //   21ef23 21efef 21ef6f 216fe7 216f21 216fcb 216f6b 216f2d 216f6e 216fee 216f23 216fef 216f6f cbe7e7
  //   cbe721 cbe7cb cbe76b cbe72d cbe76e cbe7ee cbe723 cbe7ef cbe76f cb21e7 cb2121 cb21cb cb216b cb212d
  //   cb216e cb21ee cb2123 cb21ef cb216f cbcbe7 cbcb21 cbcbcb cbcb6b cbcb2d cbcb6e cbcbee cbcb23 cbcbef
  //   cbcb6f cb6be7 cb6b21 cb6bcb cb6b6b cb6b2d cb6b6e cb6bee cb6b23 cb6bef cb6b6f cb2de7 cb2d21 cb2dcb
  //   cb2d6b cb2d2d cb2d6e cb2dee cb2d23 cb2def cb2d6f cb6ee7 cb6e21 cb6ecb cb6e6b cb6e2d cb6e6e cb6eee
  //   cb6e23 cb6eef cb6e6f cbeee7 cbee21 cbeecb cbee6b cbee2d cbee6e cbeeee cbee23 cbeeef cbee6f cb23e7
  //   cb2321 cb23cb cb236b cb232d cb236e cb23ee cb2323 cb23ef cb236f cbefe7 cbef21 cbefcb cbef6b cbef2d
  //   cbef6e cbefee cbef23 cbefef cbef6f cb6fe7 cb6f21 cb6fcb cb6f6b cb6f2d cb6f6e cb6fee cb6f23 cb6fef
  //   cb6f6f 6be7e7 6be721 6be7cb 6be76b 6be72d 6be76e 6be7ee 6be723 6be7ef 6be76f 6b21e7 6b2121 6b21cb
  //   6b216b 6b212d 6b216e 6b21ee 6b2123 6b21ef 6b216f 6bcbe7 6bcb21 6bcbcb 6bcb6b 6bcb2d 6bcb6e 6bcbee
  //   6bcb23 6bcbef 6bcb6f 6b6be7 6b6b21 6b6bcb 6b6b6b 6b6b2d 6b6b6e 6b6bee 6b6b23 6b6bef 6b6b6f 6b2de7
  //   6b2d21 6b2dcb 6b2d6b 6b2d2d 6b2d6e 6b2dee 6b2d23 6b2def 6b2d6f 6b6ee7 6b6e21 6b6ecb 6b6e6b 6b6e2d
  //   6b6e6e 6b6eee 6b6e23 6b6eef 6b6e6f 6beee7 6bee21 6beecb 6bee6b 6bee2d 6bee6e 6beeee 6bee23 6beeef
  //   6bee6f 6b23e7 6b2321 6b23cb 6b236b 6b232d 6b236e 6b23ee 6b2323 6b23ef 6b236f 6befe7 6bef21 6befcb
  //   6bef6b 6bef2d 6bef6e 6befee 6bef23 6befef 6bef6f 6b6fe7 6b6f21 6b6fcb 6b6f6b 6b6f2d 6b6f6e 6b6fee
  //   6b6f23 6b6fef 6b6f6f 2de7e7 2de721 2de7cb 2de76b 2de72d 2de76e 2de7ee 2de723 2de7ef 2de76f 2d21e7
  //   2d2121 2d21cb 2d216b 2d212d 2d216e 2d21ee 2d2123 2d21ef 2d216f 2dcbe7 2dcb21 2dcbcb 2dcb6b 2dcb2d
  //   2dcb6e 2dcbee 2dcb23 2dcbef 2dcb6f 2d6be7 2d6b21 2d6bcb 2d6b6b 2d6b2d 2d6b6e 2d6bee 2d6b23 2d6bef
  //   2d6b6f 2d2de7 2d2d21 2d2dcb 2d2d6b 2d2d2d 2d2d6e 2d2dee 2d2d23 2d2def 2d2d6f 2d6ee7 2d6e21 2d6ecb
  //   2d6e6b 2d6e2d 2d6e6e 2d6eee 2d6e23 2d6eef 2d6e6f 2deee7 2dee21 2deecb 2dee6b 2dee2d 2dee6e 2deeee
  //   2dee23 2deeef 2dee6f 2d23e7 2d2321 2d23cb 2d236b 2d232d 2d236e 2d23ee 2d2323 2d23ef 2d236f 2defe7
  //   2def21 2defcb 2def6b 2def2d 2def6e 2defee 2def23 2defef 2def6f 2d6fe7 2d6f21 2d6fcb 2d6f6b 2d6f2d
  //   2d6f6e 2d6fee 2d6f23 2d6fef 2d6f6f 6ee7e7 6ee721 6ee7cb 6ee76b 6ee72d 6ee76e 6ee7ee 6ee723 6ee7ef
  //   6ee76f 6e21e7 6e2121 6e21cb 6e216b 6e212d 6e216e 6e21ee 6e2123 6e21ef 6e216f 6ecbe7 6ecb21 6ecbcb
  //   6ecb6b 6ecb2d 6ecb6e 6ecbee 6ecb23 6ecbef 6ecb6f 6e6be7 6e6b21 6e6bcb 6e6b6b 6e6b2d 6e6b6e 6e6bee
  //   6e6b23 6e6bef 6e6b6f 6e2de7 6e2d21 6e2dcb 6e2d6b 6e2d2d 6e2d6e 6e2dee 6e2d23 6e2def 6e2d6f 6e6ee7
  //   6e6e21 6e6ecb 6e6e6b 6e6e2d 6e6e6e 6e6eee 6e6e23 6e6eef 6e6e6f 6eeee7 6eee21 6eeecb 6eee6b 6eee2d
  //   6eee6e 6eeeee 6eee23 6eeeef 6eee6f 6e23e7 6e2321 6e23cb 6e236b 6e232d 6e236e 6e23ee 6e2323 6e23ef
  //   6e236f 6eefe7 6eef21 6eefcb 6eef6b 6eef2d 6eef6e 6eefee 6eef23 6eefef 6eef6f 6e6fe7 6e6f21 6e6fcb
  //   6e6f6b 6e6f2d 6e6f6e 6e6fee 6e6f23 6e6fef 6e6f6f eee7e7 eee721 eee7cb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
endmodule

module CU2 (
  input  OP3,
  input  OP2,
  input  OP1,
  input  OP0,
  input  SC2,
  input  SC1,
  input  SC0,
  output C12,
  output C13,
  output C14,
  output C15,
  output C16,
  output C17,
  output C18,
  output C19,
  output C20,
  output C21
);

  wire and_1_out, and_2_out, and_5_out, and_6_out, and_7_out, and_8_out, and_9_out, and_10_out, and_11_out,
       not_1_out, not_2_out, not_3_out, not_4_out, not_5_out, not_6_out, not_7_out, not_8_out, not_9_out,
       not_10_out;

  not not_1 (not_1_out, OP3);
  not not_2 (not_2_out, OP0);
  not not_3 (not_3_out, SC0);
  and and_1 (and_1_out, OP0, SC2, SC0);
  and and_2 (and_2_out, OP3, SC2, SC0);
  not not_4 (not_4_out, OP2);
  not not_5 (not_5_out, OP0);
  not not_6 (not_6_out, OP1);
  not not_7 (not_7_out, OP0);
  not not_8 (not_8_out, OP1);
  not not_9 (not_9_out, OP0);
  and and_3 (C19, OP2, OP1, OP0, SC1, SC0);
  and and_4 (C20, OP3, SC1, SC0);
  not not_10 (not_10_out, SC0);
  and and_5 (and_5_out, not_1_out, not_2_out, SC2, SC0);
  and and_6 (and_6_out, OP3, SC2, not_3_out);
  or or_1 (C13, and_1_out, and_2_out);
  and and_7 (and_7_out, not_4_out, OP1, OP0, SC1, SC0);
  and and_8 (and_8_out, OP3, SC2, SC0);
  and and_9 (and_9_out, OP1, not_5_out, SC1, SC0);
  and and_10 (and_10_out, OP2, SC1, SC0);
  and and_11 (and_11_out, OP3, SC1, SC0);
  and and_12 (C16, OP2, not_6_out, not_7_out, SC1, SC0);
  and and_13 (C17, OP2, not_8_out, OP0, SC1, SC0);
  and and_14 (C18, OP2, OP1, not_9_out, SC1, SC0);
  and and_15 (C21, OP3, SC2, not_10_out);
  or or_2 (C12, and_5_out, and_6_out);
  or or_3 (C14, and_7_out, and_8_out);
  or or_4 (C15, and_9_out, and_10_out, and_11_out);
endmodule

module CU1 (
  input  OPC3,
  input  OPC2,
  input  OPC1,
  input  OPC0,
  input  SC2,
  input  SC1,
  input  SC0,
  output C0,
  output C1,
  output C2,
  output C3,
  output C4,
  output C5,
  output C6,
  output C7,
  output C8,
  output C9,
  output C10,
  output C11
);

  wire and_5_out, and_6_out, and_7_out, and_8_out, and_9_out, and_10_out, and_11_out, and_12_out, and_13_out,
       and_15_out, and_16_out, and_17_out, and_18_out, and_19_out, and_20_out, and_21_out, and_22_out,
       and_23_out, and_24_out, and_25_out, and_26_out, and_27_out, and_28_out, and_29_out, and_30_out,
       and_31_out, and_32_out, and_33_out, not_1_out, not_2_out, not_3_out, not_4_out, not_5_out, not_6_out,
       not_7_out, not_8_out, not_9_out, not_10_out, not_11_out, not_12_out, not_13_out, not_14_out,
       not_15_out, not_16_out, not_17_out, not_18_out, not_19_out, not_20_out, not_21_out, not_22_out,
       not_23_out, not_24_out, not_25_out, not_26_out, not_27_out, not_28_out, not_29_out, not_30_out,
       not_31_out, not_32_out, not_33_out, not_34_out, not_35_out, not_36_out, not_37_out, not_38_out,
       not_39_out, not_40_out, not_41_out, not_42_out, not_43_out, not_44_out, not_45_out, not_46_out,
       not_47_out, not_48_out, not_49_out;

  not not_1 (not_1_out, SC2);
  not not_2 (not_2_out, SC1);
  not not_3 (not_3_out, SC0);
  not not_4 (not_4_out, SC2);
  not not_5 (not_5_out, SC1);
  and and_1 (C2, OPC1, SC2);
  not not_6 (not_6_out, SC2);
  not not_7 (not_7_out, SC1);
  not not_8 (not_8_out, OPC1);
  not not_9 (not_9_out, SC0);
  not not_10 (not_10_out, SC2);
  not not_11 (not_11_out, SC1);
  not not_12 (not_12_out, OPC1);
  not not_13 (not_13_out, SC0);
  not not_14 (not_14_out, OPC2);
  not not_15 (not_15_out, OPC3);
  not not_16 (not_16_out, SC0);
  and and_2 (C6, OPC1, SC2);
  not not_17 (not_17_out, SC0);
  not not_18 (not_18_out, OPC3);
  not not_19 (not_19_out, OPC2);
  not not_20 (not_20_out, OPC1);
  not not_21 (not_21_out, OPC1);
  not not_22 (not_22_out, OPC2);
  not not_23 (not_23_out, OPC1);
  not not_24 (not_24_out, SC2);
  not not_25 (not_25_out, SC1);
  not not_26 (not_26_out, SC0);
  not not_27 (not_27_out, OPC3);
  not not_28 (not_28_out, OPC2);
  not not_29 (not_29_out, OPC1);
  not not_30 (not_30_out, OPC1);
  not not_31 (not_31_out, OPC2);
  not not_32 (not_32_out, OPC3);
  not not_33 (not_33_out, OPC1);
  not not_34 (not_34_out, OPC0);
  not not_35 (not_35_out, SC1);
  not not_36 (not_36_out, OPC1);
  not not_37 (not_37_out, OPC2);
  not not_38 (not_38_out, SC2);
  not not_39 (not_39_out, SC1);
  not not_40 (not_40_out, SC0);
  not not_41 (not_41_out, SC2);
  not not_42 (not_42_out, SC1);
  not not_43 (not_43_out, SC2);
  not not_44 (not_44_out, SC1);
  not not_45 (not_45_out, SC2);
  not not_46 (not_46_out, SC1);
  not not_47 (not_47_out, OPC0);
  not not_48 (not_48_out, OPC3);
  not not_49 (not_49_out, SC2);
  and and_3 (C0, not_1_out, not_2_out, not_3_out);
  and and_4 (C1, not_4_out, not_5_out, SC0);
  and and_5 (and_5_out, not_6_out, not_7_out, SC0);
  and and_6 (and_6_out, not_8_out, SC2, not_9_out);
  and and_7 (and_7_out, not_10_out, not_11_out, SC0);
  and and_8 (and_8_out, not_12_out, SC2, not_13_out);
  and and_9 (and_9_out, not_14_out, OPC1, OPC0, SC0);
  and and_10 (and_10_out, not_15_out, OPC2, SC2, SC0);
  and and_11 (and_11_out, OPC3, OPC1, OPC0, SC0);
  and and_12 (and_12_out, SC1, not_16_out);
  and and_13 (and_13_out, SC2, SC0);
  and and_14 (C7, SC1, not_17_out);
  and and_15 (and_15_out, not_18_out, not_19_out, not_20_out, SC1, SC0);
  and and_16 (and_16_out, not_21_out, SC2, SC1, SC0);
  and and_17 (and_17_out, not_22_out, OPC0, SC1, SC0);
  and and_18 (and_18_out, OPC3, OPC0, SC1, SC0);
  and and_19 (and_19_out, OPC3, OPC2, not_23_out, SC1, SC0);
  and and_20 (and_20_out, not_24_out, not_25_out, not_26_out);
  and and_21 (and_21_out, not_27_out, not_28_out, not_29_out, SC1, SC0);
  and and_22 (and_22_out, not_30_out, SC2, SC1, SC0);
  and and_23 (and_23_out, not_31_out, OPC0, SC1, SC0);
  and and_24 (and_24_out, not_32_out, OPC2, not_33_out, not_34_out, not_35_out);
  and and_25 (and_25_out, OPC3, OPC0, SC1, SC0);
  and and_26 (and_26_out, OPC3, OPC2, not_36_out, SC1, SC0);
  and and_27 (and_27_out, not_37_out, not_38_out, not_39_out, SC0);
  and and_28 (and_28_out, SC2, not_40_out);
  and and_29 (and_29_out, OPC0, not_41_out, not_42_out, SC0);
  and and_30 (and_30_out, OPC1, not_43_out, not_44_out, SC0);
  and and_31 (and_31_out, OPC3, not_45_out, not_46_out, SC0);
  and and_32 (and_32_out, OPC1, not_47_out, SC1, SC0);
  and and_33 (and_33_out, not_48_out, OPC2, not_49_out, SC1, SC0);
  or or_1 (C3, and_5_out, and_6_out);
  or or_2 (C4, and_7_out, and_8_out, and_9_out, and_10_out, and_11_out);
  or or_3 (C5, and_12_out, and_13_out);
  or or_4 (C8, and_15_out, and_16_out, and_17_out, and_18_out, and_19_out);
  or or_5 (C9, and_20_out, and_21_out, and_22_out, and_23_out, and_24_out, and_25_out, and_26_out);
  or or_6 (C10, and_27_out, and_28_out, and_29_out, and_30_out, and_31_out);
  or or_7 (C11, and_32_out, and_33_out);
endmodule

module improved_Adder (
  input  XOR,
  input  AND,
  input  OR,
  input  Subtract,
  input  [7:0] B,
  input  [7:0] A,
  input  OE,
  output [7:0] Dout,
  output [7:0] Stored_Data,
  output Cout
);

  wire or_2_out, should_add;
  wire [7:0] adder_1_out, and_1_out, bit_extender_1_out, or_1_out, xor_1_out, xor_2_out;

  assign bit_extender_1_out = {{7{Subtract}}, Subtract};  // Bit_Extender bit_extender_1
  assign xor_1_out = bit_extender_1_out ^ B;  // XOR_Gate xor_1, 8 bits wide
  assign or_1_out = A | B;  // OR_Gate or_1, 8 bits wide
  assign and_1_out = B & A;  // AND_Gate and_1, 8 bits wide
  assign xor_2_out = B ^ A;  // XOR_Gate xor_2, 8 bits wide
  Adder adder_1 (.a(xor_1_out), .b(A), .out(adder_1_out), .cin(Subtract), .cout(Cout));
  nor nor_1 (should_add, OR, AND, Subtract, XOR);
  or or_2 (or_2_out, should_add, Subtract);
  assign Stored_Data = OR ? or_1_out : 8'bz;  // Controlled_Buffer controlled_buffer_1
  assign Stored_Data = or_2_out ? adder_1_out : 8'bz;  // Controlled_Buffer controlled_buffer_2
  assign Stored_Data = AND ? and_1_out : 8'bz;  // Controlled_Buffer controlled_buffer_3
  assign Stored_Data = XOR ? xor_2_out : 8'bz;  // Controlled_Buffer controlled_buffer_4
  assign Dout = OE ? Stored_Data : 8'bz;  // Controlled_Buffer controlled_buffer_5
endmodule

module Output_Register (
  input  Clock,
  input  WE,
  input  [7:0] Din,
  input  OE,
  input  RESET,
  input  INC,
  input  CMP,
  input  SHL,
  input  SHR,
  output [7:0] Dout,
  output [7:0] Stored_Data
);

  wire act_as_register;
  wire [7:0] adder_1_out, controlled_buffer_1_out, not_1_out, shifter_1_out, shifter_2_out;

  assign controlled_buffer_1_out = act_as_register ? Din : 8'bz;  // Controlled_Buffer controlled_buffer_1
  assign not_1_out = ~Din;  // NOT_Gate not_1, 8 bits wide
  Shifter shifter_1 (.in(Din), .\dist (3'b001), .out(shifter_1_out));
  Shifter #(.shift("lr")) shifter_2 (.in(Din), .\dist (3'b001), .out(shifter_2_out));
  Adder adder_1 (.a(Din), .b({8{1'b0}}), .out(adder_1_out), .cin(1'b1));  // open: cout
  assign controlled_buffer_1_out = INC ? adder_1_out : 8'bz;  // Controlled_Buffer controlled_buffer_2
  assign adder_1_out = CMP ? not_1_out : 8'bz;  // Controlled_Buffer controlled_buffer_3
  assign not_1_out = SHL ? shifter_1_out : 8'bz;  // Controlled_Buffer controlled_buffer_4
  assign shifter_1_out = SHR ? shifter_2_out : 8'bz;  // Controlled_Buffer controlled_buffer_5
  register register_1 (
    .Clock(Clock), .WE(WE), .Din(controlled_buffer_1_out), .OE(OE), .Reset(RESET), .Dout(Dout),
    .Stored_Data(Stored_Data));
  nor nor_1 (act_as_register, INC, CMP, SHL, SHR);
endmodule
